# Fritzing sketch MICRO_Adafruit_GPS (saved by Fritzing 0.8.7b)
breadboards: 1

parts:
  ARDUINO1 = Arduino Micro
  GPS1 = Adafruit Ultimate GPS Breakout

nets:
  N1: ARDUINO1.TX, GPS1.RX
  N2: ARDUINO1.RX, GPS1.TX
  N3: ARDUINO1.GND#6, GPS1.GND
  5V: ARDUINO1.5V, GPS1.VIN

notes:
  Arduino MICRO and Adafruit's Ultimate GPS chipset. brycej 02/24/2014

custom parts:
  Arduino Micro: Arduino Micro Microcontroller
